// Logisim project lab1.circ as structural Verilog: 8 circuits, main circuit Main (DO NOT MODIFY)
module Main__DO_NOT_MODIFY (
);

  wire _3_Bit_Enable, _4_Bit_Enable, _8_Bit_Enable, a, a_prime, b, b_prime, c, c_prime, CIN, Clock,
       comparator_1_eq, comparator_2_eq, comparator_3_eq, comparator_4_eq, comparator_5_eq, comparator_6_eq,
       comparator_7_eq, comparator_8_eq, comparator_9_eq, comparator_10_eq, counter_1_carry, counter_3_carry,
       counter_4_carry, d, d_prime, e, e_prime, even_parity_1_out, f, f_prime, g, g_prime, multiplexer_1_out,
       n1_quick_introduction_to_logisim_1_f, n1_quick_introduction_to_logisim_1_g, n2_karnaugh_map_1_f,
       n5_mux_function_implementation_1_f, n6_parity_checker_1_parity, or_1_out, rom_1_data, rom_3_data,
       rom_7_data, rom_8_data;
  wire [1:0] Selector_Bits;
  wire [2:0] _3_Bit_Counter, A_Operand, B_Operand, C_Correct_Output, Your_Output;
  wire [3:0] _4_Bit_Counter, _9_Counter, n4_bit_counting_1_output, rom_2_data;
  wire [6:0] adder_1_out, adder_2_out, bit_extender_1_out, bit_extender_2_out;
  wire [7:0] _8_Bit_Counter;

  Clock clock_1 (.out(Clock));
  Counter #(.width(4), .max('hf), .ongoal("stay")) counter_1 (
    .count(1'b1), .Q(_4_Bit_Counter), .carry(counter_1_carry), .clk(Clock));  // open: load, D, clr
  not not_1 (_4_Bit_Enable, counter_1_carry);
  Counter #(.width(4), .max('h9), .ongoal("stay")) counter_2 (
    .count(1'b1), .Q(_9_Counter), .clk(Clock));  // open: load, D, carry, clr
  Counter #(.ongoal("stay")) counter_3 (
    .count(1'b1), .Q(_8_Bit_Counter), .carry(counter_3_carry), .clk(Clock));  // open: load, D, clr
  not not_2 (_8_Bit_Enable, counter_3_carry);
  Counter #(.width(3), .max('h7), .ongoal("stay")) counter_4 (
    .count(1'b1), .Q(_3_Bit_Counter), .carry(counter_4_carry), .clk(Clock));  // open: load, D, clr
  not not_3 (_3_Bit_Enable, counter_4_carry);
  _2_Karnaugh_map u_2_karnaugh_map_1 (
    .A(_4_Bit_Counter[3]), .B(_4_Bit_Counter[2]), .C(_4_Bit_Counter[1]), .D(_4_Bit_Counter[0]),
    .f(n2_karnaugh_map_1_f));
  _3_Seven_segment_display u_3_seven_segment_display_1 (
    .w3(_9_Counter[3]), .w2(_9_Counter[2]), .w0(_9_Counter[0]), .a(a_prime), .b(b_prime), .c(c_prime),
    .d(d_prime), .e(e_prime), .f(f_prime), .g(g_prime), .w1(_9_Counter[1]));
  _4_Bit_counting u_4_bit_counting_1 (
    ._7(_8_Bit_Counter[7]), ._6(_8_Bit_Counter[6]), ._5(_8_Bit_Counter[5]), ._4(_8_Bit_Counter[4]),
    ._3(_8_Bit_Counter[3]), ._2(_8_Bit_Counter[2]), ._1(_8_Bit_Counter[1]), ._0(_8_Bit_Counter[0]),
    .Output(n4_bit_counting_1_output));
  _5_MUX_function_implementation u_5_mux_function_implementation_1 (
    .a(_3_Bit_Counter[2]), .b(_3_Bit_Counter[1]), .c(_3_Bit_Counter[0]),
    .f(n5_mux_function_implementation_1_f));
  _6_Parity_checker u_6_parity_checker_1 (
    ._7(_8_Bit_Counter[7]), ._6(_8_Bit_Counter[6]), ._5(_8_Bit_Counter[5]), ._4(_8_Bit_Counter[4]),
    ._3(_8_Bit_Counter[3]), ._2(_8_Bit_Counter[2]), ._1(_8_Bit_Counter[1]), ._0(_8_Bit_Counter[0]),
    .Parity(n6_parity_checker_1_parity));
  _7_3_bit_ALU u_7_3_bit_alu_1 (
    .A2(A_Operand[2]), .A1(A_Operand[1]), .A0(A_Operand[0]), .B2(B_Operand[2]), .B1(B_Operand[1]),
    .B0(B_Operand[0]), .S1(Selector_Bits[1]), .S0(Selector_Bits[0]), .CIN(CIN), .C2(Your_Output[2]),
    .C1(Your_Output[1]), .C0(Your_Output[0]));
  _1_Quick_introduction_to_Logisim u_1_quick_introduction_to_logisim_1 (
    .A(_4_Bit_Counter[3]), .B(_4_Bit_Counter[2]), .C(_4_Bit_Counter[1]),
    .f(n1_quick_introduction_to_logisim_1_f), .D(_4_Bit_Counter[0]), .g(n1_quick_introduction_to_logisim_1_g));
  _1_Quick_introduction_to_Logisim u_1_quick_introduction_to_logisim_2 ();  // open: A, B, C, f, D, g
  Comparator #(.width(4)) comparator_1 (.a(4'b0010), .b(_4_Bit_Counter), .eq(comparator_1_eq));  // open: gt, lt
  Comparator #(.width(4)) comparator_2 (.a(4'b0111), .b(_4_Bit_Counter), .eq(comparator_2_eq));  // open: gt, lt
  Comparator #(.width(4)) comparator_3 (.a(4'b1000), .b(_4_Bit_Counter), .eq(comparator_3_eq));  // open: gt, lt
  ROM #(.addrWidth(4), .dataWidth(1)) rom_1 (.addr(_4_Bit_Counter), .data(rom_1_data));  // open: sel
  ROM #(.dataWidth(4)) rom_2 (.addr(_8_Bit_Counter), .data(rom_2_data));  // open: sel
  ROM #(.addrWidth(3), .dataWidth(1)) rom_3 (.addr(_3_Bit_Counter), .data(rom_3_data));  // open: sel
  xnor even_parity_1 (even_parity_1_out, _8_Bit_Counter[7], _8_Bit_Counter[6], _8_Bit_Counter[5], _8_Bit_Counter[4], _8_Bit_Counter[3], _8_Bit_Counter[2], _8_Bit_Counter[1], _8_Bit_Counter[0]);
  ROM #(.addrWidth(4), .dataWidth(3)) rom_4 (.addr(_4_Bit_Counter), .data(A_Operand));  // open: sel
  ROM #(.addrWidth(4), .dataWidth(2)) rom_5 (.addr(_4_Bit_Counter), .data(Selector_Bits));  // open: sel
  ROM #(.addrWidth(4), .dataWidth(1)) rom_6 (.addr(_4_Bit_Counter), .data(CIN));  // open: sel
  ROM #(.addrWidth(4), .dataWidth(1)) rom_7 (.addr(_4_Bit_Counter), .data(rom_7_data));  // open: sel
  ROM #(.addrWidth(4), .dataWidth(1)) rom_8 (.addr(_4_Bit_Counter), .data(rom_8_data));  // open: sel
  or or_1 (or_1_out, comparator_1_eq, comparator_2_eq, comparator_3_eq);
  Comparator #(.width(1)) comparator_4 (.a(n2_karnaugh_map_1_f), .b(rom_1_data), .eq(comparator_4_eq));  // open: gt, lt
  ROM #(.addrWidth(4), .dataWidth(7)) rom_9 (.addr(_9_Counter), .data({a, b, c, d, e, f, g}));  // open: sel
  Comparator #(.width(4)) comparator_5 (
    .a(rom_2_data), .b(n4_bit_counting_1_output), .eq(comparator_5_eq));  // open: gt, lt
  Comparator #(.width(1)) comparator_6 (
    .a(even_parity_1_out), .b(n6_parity_checker_1_parity), .eq(comparator_6_eq));  // open: gt, lt
  Comparator #(.width(1)) comparator_7 (
    .a(rom_7_data), .b(n1_quick_introduction_to_logisim_1_f), .eq(comparator_7_eq));  // open: gt, lt
  Comparator #(.width(1)) comparator_8 (
    .a(n1_quick_introduction_to_logisim_1_g), .b(rom_8_data), .eq(comparator_8_eq));  // open: gt, lt
  Multiplexer #(.enable("false")) multiplexer_1 (
    .in0(comparator_4_eq), .in1(1'b1), .out(multiplexer_1_out), .sel(or_1_out));
  assign bit_extender_1_out = {{6{1'b0}}, comparator_5_eq};  // Bit_Extender bit_extender_1
  Comparator #(.width(1)) comparator_9 (
    .a(rom_3_data), .b(n5_mux_function_implementation_1_f), .eq(comparator_9_eq));  // open: gt, lt
  assign bit_extender_2_out = {{6{1'b0}}, comparator_6_eq};  // Bit_Extender bit_extender_2
  Adder #(.width(7)) adder_1 (.a(bit_extender_1_out), .b(7'b0110000), .out(adder_1_out));  // open: cin, cout
  Adder #(.width(7)) adder_2 (.a(bit_extender_2_out), .b(7'b0110000), .out(adder_2_out));  // open: cin, cout
  ROM #(.addrWidth(4), .dataWidth(3)) rom_10 (.addr(_4_Bit_Counter), .data(B_Operand));  // open: sel
  ROM #(.addrWidth(4), .dataWidth(3)) rom_11 (.addr(_4_Bit_Counter), .data(C_Correct_Output));  // open: sel
  Shift_Register #(.length(15)) shift_register_1 (
    .shift(_4_Bit_Enable), .in(comparator_7_eq), .clk(Clock));  // open: out, load, clr, d0, q0, d1, q1, d2, q2, d3, q3, d4, q4, d5, q5, d6, q6, d7, q7, d8, q8, d9, q9, d10, q10, d11, q11, d12, q12, d13, q13, d14, q14
  Shift_Register #(.length(15)) shift_register_2 (
    .shift(_4_Bit_Enable), .in(comparator_8_eq), .clk(Clock));  // open: out, load, clr, d0, q0, d1, q1, d2, q2, d3, q3, d4, q4, d5, q5, d6, q6, d7, q7, d8, q8, d9, q9, d10, q10, d11, q11, d12, q12, d13, q13, d14, q14
  Shift_Register #(.length(15)) shift_register_3 (
    .shift(_4_Bit_Enable), .in(multiplexer_1_out), .clk(Clock));  // open: out, load, clr, d0, q0, d1, q1, d2, q2, d3, q3, d4, q4, d5, q5, d6, q6, d7, q7, d8, q8, d9, q9, d10, q10, d11, q11, d12, q12, d13, q13, d14, q14
  _7_Segment_Display u_7_segment_display_1 (.g(g), .f(f), .a(a), .b(b), .e(e), .d(d), .c(c));  // open: dp
  TTY tty_1 (.data(adder_1_out), .clk(Clock), .we(_8_Bit_Enable));  // open: clr
  Shift_Register #(.length(7)) shift_register_4 (
    .shift(_3_Bit_Enable), .in(comparator_9_eq), .clk(Clock));  // open: out, load, clr, d0, q0, d1, q1, d2, q2, d3, q3, d4, q4, d5, q5, d6, q6
  TTY tty_2 (.data(adder_2_out), .clk(Clock), .we(_8_Bit_Enable));  // open: clr
  Comparator #(.width(3)) comparator_10 (.a(C_Correct_Output), .b(Your_Output), .eq(comparator_10_eq));  // open: gt, lt
  // Probe on comparator_9_eq
  // Probe on comparator_7_eq
  // Probe on comparator_8_eq
  _7_Segment_Display u_7_segment_display_2 (
    .g(g_prime), .f(f_prime), .a(a_prime), .b(b_prime), .e(e_prime), .d(d_prime), .c(c_prime));  // open: dp
  Shift_Register #(.length(15)) shift_register_5 (
    .shift(_4_Bit_Enable), .in(comparator_10_eq), .clk(Clock));  // open: out, load, clr, d0, q0, d1, q1, d2, q2, d3, q3, d4, q4, d5, q5, d6, q6, d7, q7, d8, q8, d9, q9, d10, q10, d11, q11, d12, q12, d13, q13, d14, q14
  // Probe on multiplexer_1_out
  // Probe on comparator_5_eq
  // Probe on comparator_6_eq
  // Probe on comparator_10_eq
  // Probe on A_Operand
  // Probe on Selector_Bits
  // Probe on B_Operand
  // Probe on A_Operand
  // Probe on B_Operand
  // Probe on CIN
  // Probe on CIN
  // Probe on C_Correct_Output
  // Probe on C_Correct_Output
  // Probe on Your_Output
  // Probe on Your_Output

  // Notes on the sheet:
  //   A Operand
  //   Selector Bits
  //   CIN
  //   contents of rom_1 (hex, n*v repeats v):
  //   0 0 1 1 0 1 0 1 1 1 0 0 1 1
  //   contents of rom_2 (hex, n*v repeats v):
  //   0 1 1 2 1 2 2 3 1 2 2 3 2 3 3 4 1 2 2 3 2 3 3 4 2 3 3 4 3 4 4 5 1 2 2 3 2 3 3 4 2 3 3 4 3 4 4 5 2 3
  //   3 4 3 4 4 5 3 4 4 5 4 5 5 6 1 2 2 3 2 3 3 4 2 3 3 4 3 4 4 5 2 3 3 4 3 4 4 5 3 4 4 5 4 5 5 6 2 3 3 4
  //   3 4 4 5 3 4 4 5 4 5 5 6 3 4 4 5 4 5 5 6 4 5 5 6 5 6 6 7 1 2 2 3 2 3 3 4 2 3 3 4 3 4 4 5 2 3 3 4 3 4
  //   4 5 3 4 4 5 4 5 5 6 2 3 3 4 3 4 4 5 3 4 4 5 4 5 5 6 3 4 4 5 4 5 5 6 4 5 5 6 5 6 6 7 2 3 3 4 3 4 4 5
  //   3 4 4 5 4 5 5 6 3 4 4 5 4 5 5 6 4 5 5 6 5 6 6 7 3 4 4 5 4 5 5 6 4 5 5 6 5 6 6 7 4 5 5 6 5 6 6 7 5 6
  //   6 7 6 7 7 8
  //   contents of rom_3 (hex, n*v repeats v):
  //   1 0 1 0 1 0 1
  //   contents of rom_4 (hex, n*v repeats v):
  //   0 5 1 6 2 7 2 7 3 0 1 2 7 7 1 1
  //   contents of rom_5 (hex, n*v repeats v):
  //   0 0 0 1 1 1 2 2 2 7*3
  //   contents of rom_6 (hex, n*v repeats v):
  //   9*0 1 1 4*0 1
  //   contents of rom_7 (hex, n*v repeats v):
  //   6*0 1 0 1 1 0 0 1 0 1 1
  //   contents of rom_8 (hex, n*v repeats v):
  //   4*0 1 1 0 7*1 0 1
  //   contents of rom_9 (hex, n*v repeats v):
  //   7e 30 6d 79 33 5b 5f 70 7f 7b
  //   B Operand
  //   C Correct Output
  //   contents of rom_10 (hex, n*v repeats v):
  //   5 7 2 2 1 6 5 7 1 0 1 1 7 6 7 4
  //   contents of rom_11 (hex, n*v repeats v):
  //   5 2 3 6 3 7 0 7 1 1 3 3 6 5 0 6
  //   TTY will be filled with 1s (except for bottom right corner) and last input will be 1 when done correctly
  //   TTY will be filled with 1s (except for bottom right corner) and last input will be 1 when done correctly
  //   Both shift registers and last inputs will be all 1s when done correctly
  //   The shift register and the last input will be all 1s when done correctly
  //   The shift register and the last input will be all 1s when done correctly
  //   Display on right should exactly match display on left on every tick
  //   The shift register and the last input will be all 1s when done correctly
  //   Ctrl-T to tick once
  //   Ctrl-R to reset the simulation
  //   Ctrl-K to run the simulation at the tick speed in Simulate -> Tick Frequency
  //   00 = XOR
  //   01 = OR
  //   10 = AND
  //   11 = ADD/SUB
  //   For ADD/SUB, look here for signed probes
  //   +
  //   +
  //   =
endmodule

module _1_Quick_introduction_to_Logisim (
  input  A,
  input  B,
  input  C,
  input  D,
  output f,
  output g
);

  wire A_nB_nC_out, A_nB_out, AB_nD_out, ABC_out, B_nC_out, BC_nD_out, BD_out, nB_2_out, nB_out, nC_2_out,
       nC_out, nD_out;

  not nB (nB_out, B);
  not nC (nC_out, C);
  not nD (nD_out, D);
  not nB_2 (nB_2_out, B);
  not nC_2 (nC_2_out, C);
  and A_nB_nC (A_nB_nC_out, A, nB_out, nC_out);
  and AB_nD (AB_nD_out, A, B, nD_out);
  and BC_nD (BC_nD_out, B, C, nD_out);
  and ABC (ABC_out, A, B, C);
  and A_nB (A_nB_out, A, nB_2_out);
  and B_nC (B_nC_out, B, nC_2_out);
  and BD (BD_out, B, D);
  or or_1 (f, A_nB_nC_out, AB_nD_out, BC_nD_out, ABC_out);
  or or_2 (g, A_nB_out, B_nC_out, BD_out);
endmodule

module _2_Karnaugh_map (
  input  A,
  input  B,
  input  C,
  input  D,
  output f
);

  wire and_1_out, and_2_out, and_3_out, and_4_out, not_1_out, not_2_out, not_3_out;

  not not_1 (not_1_out, A);
  and and_1 (and_1_out, not_1_out, C, D);
  not not_2 (not_2_out, C);
  not not_3 (not_3_out, C);
  and and_2 (and_2_out, A, B, not_2_out);
  and and_3 (and_3_out, B, not_2_out, D);
  and and_4 (and_4_out, A, not_3_out, D);
  or or_1 (f, and_1_out, and_2_out, and_3_out, and_4_out);
endmodule

module _3_Seven_segment_display (
  input  w3,
  input  w2,
  input  w1,
  input  w0,
  output a,
  output b,
  output c,
  output d,
  output e,
  output f,
  output g
);
endmodule

module _4_Bit_counting (
  input  _7,
  input  _6,
  input  _5,
  input  _4,
  input  _3,
  input  _2,
  input  _1,
  input  _0,
  output [3:0] Output
);
endmodule

module _5_MUX_function_implementation (
  input  a,
  input  b,
  input  c,
  output f
);
endmodule

module _6_Parity_checker (
  input  _7,
  input  _6,
  input  _5,
  input  _4,
  input  _3,
  input  _2,
  input  _1,
  input  _0,
  output Parity
);
endmodule

module _7_3_bit_ALU (
  input  A2,
  input  A1,
  input  A0,
  input  B2,
  input  B1,
  input  B0,
  input  S1,
  input  S0,
  input  CIN,
  output C2,
  output C1,
  output C0
);
endmodule
